// Logisim project Ctl_Load_Store.circ as structural Verilog: 1 circuit, main circuit Load_Store
module Load_Store (
  input  Clk,
  input  Reset,
  input  Enable,
  input  [31:0] Stack_Pointer,
  input  [15:0] Instruction,
  output PC_Hold,
  output Load,
  output Store,
  output [2:0] Rmd,
  output [31:0] RAM_Addr
);

  wire and_1_out, and_2_out, and_3_out, d_ff_1_q, d_ff_1_qn, not_1_out, not_2_out, or_1_out;
  wire [31:0] adder_1_out, bit_extender_1_out;

  and and_1 (and_1_out, Instruction[11], ~d_ff_1_q);  // AND_Gate
  D_Flip_Flop d_ff_1 (.D(and_1_out), .clk(not_1_out), .Q(d_ff_1_q), .Qn(d_ff_1_qn), .reset(or_1_out));  // open: preset
  not not_1 (not_1_out, Clk);
  or or_1 (or_1_out, Reset, ~Enable, ~Instruction[11]);  // OR_Gate
  assign bit_extender_1_out = {{24{1'b0}}, Instruction[7:0]};  // Bit_Extender bit_extender_1
  Adder #(.width(32)) adder_1 (.a(Stack_Pointer), .b(bit_extender_1_out), .out(adder_1_out));  // open: cin, cout
  Multiplexer #(.enable("false"), .width(32)) multiplexer_1 (
    .in0({32{1'b0}}), .in1(adder_1_out), .out(RAM_Addr), .sel(Enable));
  and and_2 (and_2_out, d_ff_1_qn, Instruction[11]);
  and and_3 (and_3_out, Instruction[11], d_ff_1_q);
  not not_2 (not_2_out, Instruction[11]);
  Multiplexer #(.enable("false")) multiplexer_2 (.in0(1'b0), .in1(and_2_out), .out(PC_Hold), .sel(Enable));
  Multiplexer #(.enable("false")) multiplexer_3 (.in0(1'b0), .in1(and_3_out), .out(Load), .sel(Enable));
  Multiplexer #(.enable("false")) multiplexer_4 (.in0(1'b0), .in1(not_2_out), .out(Store), .sel(Enable));
  Multiplexer #(.enable("false"), .width(3)) multiplexer_5 (
    .in0(3'b000), .in1(Instruction[10:8]), .out(Rmd), .sel(Enable));

  // Notes on the sheet:
  //   Instruction: pull=down
  //   Delay load and hold PC for 1 cycle for the RAM to send out requested data 
endmodule
